// Logisim project ESF.circ as structural Verilog: 13 circuits, main circuit main
module main (
  output [31:0] out_1,
  output [31:0] out_2
);

  wire and_1_out, and_2_out, and_3_out, clock_1_out, multiplexer_1_out, multiplexer_2_out;
  wire [2:0] counter_2_q;
  wire [4:0] adder_1_out, counter_1_q, subtractor_1_out;
  wire [15:0] keyschedule_1_out_5, multiplexer_12_out, multiplexer_12_out_2, register_5_q, register_5_q_2,
       register_8_q;
  wire [31:0] keyschedule_1_out_6, keyschedule_1_out_7, multiplexer_3_out, multiplexer_4_out,
       multiplexer_6_out, multiplexer_7_out, multiplexer_9_out, multiplexer_11_out, multiplexer_13_out,
       multiplexer_14_out, n7shift_1_out_2, ram_1_data, register_1_q, register_2_q, register_3_q,
       register_4_q, register_6_q, register_7_q, register_9_q, register_10_q, round_box_1_out_3, xor_1_out;
  wire [31:16] multiplexer_10_out;

  Multiplexer #(.enable("false")) multiplexer_1 (
    .in0(1'b0), .in1(clock_1_out), .out(multiplexer_1_out), .sel(and_1_out));
  and and_1 (and_1_out, counter_2_q[2], counter_2_q[1], ~counter_2_q[0]);  // AND_Gate
  Multiplexer #(.enable("false")) multiplexer_2 (
    .in0(multiplexer_1_out), .in1(1'b1), .out(multiplexer_2_out), .sel(and_2_out));
  Clock clock_1 (.out(clock_1_out));
  Counter #(.width(5), .max('h1f)) counter_1 (
    .D(counter_1_q), .count(1'b1), .Q(counter_1_q), .clk(multiplexer_2_out));  // open: load, carry, clr
  and and_2 (and_2_out, counter_1_q[4], counter_1_q[3], counter_1_q[2], counter_1_q[1], counter_1_q[0]);
  Subtractor #(.width(5)) subtractor_1 (.a({5{1'b1}}), .b(counter_1_q), .out(subtractor_1_out));  // open: bin, bout
  and and_3 (and_3_out, subtractor_1_out[0], subtractor_1_out[1], subtractor_1_out[2], subtractor_1_out[3], subtractor_1_out[4]);
  Adder #(.width(5)) adder_1 (.a(counter_1_q), .b(5'b00001), .out(adder_1_out));  // open: cin, cout
  // Probe on adder_1_out
  Counter #(.width(3), .max('h6), .ongoal("stay"), .trigger("falling")) counter_2 (
    .D(counter_2_q), .count(1'b1), .Q(counter_2_q), .clk(clock_1_out));  // open: load, carry, clr
  Register #(.width(32)) register_1 (
    .D(multiplexer_7_out), .Q(register_1_q), .clk(multiplexer_2_out));  // open: en, clr
  Multiplexer #(.select(3), .width(32), .enable("false")) multiplexer_3 (
    .in1(ram_1_data), .out(multiplexer_3_out), .sel(counter_2_q));  // open: in0, in2, in3, in4, in5, in6, in7
  Register #(.width(32)) register_2 (.D(multiplexer_3_out), .Q(register_2_q), .clk(clock_1_out));  // open: en, clr
  Multiplexer #(.width(32), .enable("false")) multiplexer_4 (
    .in0(register_1_q), .in1(register_2_q), .out(multiplexer_4_out), .sel(and_3_out));
  _7Shift u_7shift_1 (.in_1(multiplexer_4_out), .out_2(n7shift_1_out_2));
  assign xor_1_out = n7shift_1_out_2 ^ round_box_1_out_3;  // XOR_Gate xor_1, 32 bits wide
  Multiplexer #(.width(32), .enable("false")) multiplexer_5 (
    .in1(xor_1_out), .out(out_1), .sel(and_2_out));  // open: in0
  Multiplexer #(.select(3), .width(32), .enable("false")) multiplexer_6 (
    .in0(ram_1_data), .out(multiplexer_6_out), .sel(counter_2_q));  // open: in1, in2, in3, in4, in5, in6, in7
  Multiplexer #(.width(32), .enable("false")) multiplexer_7 (
    .in0(register_4_q), .in1(register_3_q), .out(multiplexer_7_out), .sel(and_3_out));
  Round_box round_box_1 (
    .out_3(round_box_1_out_3), .in_1(multiplexer_7_out), .in_2({multiplexer_10_out, multiplexer_12_out_2}));
  Multiplexer #(.width(32), .enable("false")) multiplexer_8 (
    .in1(multiplexer_7_out), .out(out_2), .sel(and_2_out));  // open: in0
  RAM #(.addrWidth(3), .dataWidth(32)) ram_1 (
    .addr(counter_2_q), .data(ram_1_data), .clk(clock_1_out));  // open: sel, ld, clr
  Register #(.width(32), .trigger("falling")) register_3 (
    .D(multiplexer_6_out), .Q(register_3_q), .clk(clock_1_out));  // open: en, clr
  Register #(.width(32)) register_4 (.D(xor_1_out), .Q(register_4_q), .clk(multiplexer_2_out));  // open: en, clr
  Multiplexer #(.select(3), .width(32), .enable("false")) multiplexer_9 (
    .in4(ram_1_data), .out(multiplexer_9_out), .sel(counter_2_q));  // open: in0, in1, in2, in3, in5, in6, in7
  Register #(.width(32)) register_5 (
    .D(multiplexer_9_out), .Q({register_5_q_2, register_5_q}), .clk(clock_1_out));  // open: en, clr
  Multiplexer #(.width(16), .enable("false")) multiplexer_10 (
    .in0(register_8_q), .in1(register_5_q), .out(multiplexer_10_out), .sel(and_3_out));
  Multiplexer #(.select(3), .width(32), .enable("false")) multiplexer_11 (
    .in3(ram_1_data), .out(multiplexer_11_out), .sel(counter_2_q));  // open: in0, in1, in2, in4, in5, in6, in7
  Register #(.width(32)) register_6 (.D(multiplexer_11_out), .Q(register_6_q), .clk(clock_1_out));  // open: en, clr
  Multiplexer #(.width(32), .enable("false")) multiplexer_12 (
    .in0(register_9_q), .in1(register_6_q), .out({multiplexer_12_out_2, multiplexer_12_out}), .sel(and_3_out));
  KeySchedule keyschedule_1 (
    .in_1(multiplexer_10_out), .in_2({multiplexer_12_out_2, multiplexer_12_out}), .in_3(multiplexer_14_out),
    .out_5(keyschedule_1_out_5), .out_6(keyschedule_1_out_6), .out_7(keyschedule_1_out_7), .in_4(adder_1_out));
  Multiplexer #(.select(3), .width(32), .enable("false")) multiplexer_13 (
    .in2(ram_1_data), .out(multiplexer_13_out), .sel(counter_2_q));  // open: in0, in1, in3, in4, in5, in6, in7
  Register #(.width(32)) register_7 (.D(multiplexer_13_out), .Q(register_7_q), .clk(clock_1_out));  // open: en, clr
  Multiplexer #(.width(32), .enable("false")) multiplexer_14 (
    .in0(register_10_q), .in1(register_7_q), .out(multiplexer_14_out), .sel(and_3_out));
  Register #(.width(16)) register_8 (
    .D(keyschedule_1_out_5), .Q(register_8_q), .clk(multiplexer_2_out));  // open: en, clr
  Register #(.width(32)) register_9 (
    .D(keyschedule_1_out_6), .Q(register_9_q), .clk(multiplexer_2_out));  // open: en, clr
  Register #(.width(32)) register_10 (
    .D(keyschedule_1_out_7), .Q(register_10_q), .clk(multiplexer_2_out));  // open: en, clr
endmodule

module Round_box (
  input  [31:0] in_1,
  input  [31:0] in_2,
  output [31:0] out_3
);

  wire [3:0] s3_1_out_2, s4_1_out_2, s5_1_out_2, s6_1_out_2, s7_1_out_2, xor_1_out_2, xor_1_out_3,
       xor_1_out_4, xor_1_out_5;
  wire [11:0] s0_1_out_2;
  wire [15:0] xor_1_out;

  S7 s7_1 (.in_1(xor_1_out_5), .out_2(s7_1_out_2));
  S6 s6_1 (.in_1(xor_1_out_4), .out_2(s6_1_out_2));
  S5 s5_1 (.in_1(xor_1_out_3), .out_2(s5_1_out_2));
  assign {xor_1_out_5, xor_1_out_4, xor_1_out_3, xor_1_out_2, xor_1_out} = in_2 ^ in_1;  // XOR_Gate xor_1, 32 bits wide
  S4 s4_1 (.in_1(xor_1_out_2), .out_2(s4_1_out_2));
  P_Box p_box_1 (
    .in_1({s7_1_out_2, s6_1_out_2}), .in_2({s5_1_out_2, s4_1_out_2}), .in_3({s3_1_out_2, s0_1_out_2[11:8]}),
    .in_4(s0_1_out_2[7:0]), .out_5(out_3));
  S3 s3_1 (.in_1(xor_1_out[15:12]), .out_2(s3_1_out_2));
  S2 s2_1 (.in_1(xor_1_out[11:8]), .out_2(s0_1_out_2[11:8]));
  S1 s1_1 (.in_1(xor_1_out[7:4]), .out_2(s0_1_out_2[7:4]));
  S0 s0_1 (.in_1(xor_1_out[3:0]), .out_2(s0_1_out_2[3:0]));
endmodule

module S0 (
  input  [3:0] in_1,
  output [3:0] out_2
);

  wire and_1_out, and_2_out, and_3_out, and_4_out, and_5_out, and_6_out, and_7_out, and_8_out, and_9_out,
       and_10_out, and_11_out, and_12_out, and_13_out, and_14_out, and_15_out, and_16_out, and_17_out,
       and_18_out, and_19_out, and_20_out, not_1_out, not_2_out, not_3_out, not_4_out, not_5_out, not_6_out,
       not_7_out, not_8_out, not_9_out, not_10_out, not_11_out, not_12_out, not_13_out, not_14_out,
       not_15_out, not_16_out, not_17_out, not_18_out, not_19_out, not_20_out, not_21_out, not_22_out,
       not_23_out, not_24_out, not_25_out, not_26_out, not_27_out, not_28_out, not_29_out, not_30_out,
       not_31_out, not_32_out, not_33_out, not_34_out;

  not not_1 (not_1_out, in_1[2]);
  not not_2 (not_2_out, in_1[1]);
  not not_3 (not_3_out, in_1[3]);
  not not_4 (not_4_out, in_1[2]);
  not not_5 (not_5_out, in_1[0]);
  not not_6 (not_6_out, in_1[3]);
  not not_7 (not_7_out, in_1[1]);
  not not_8 (not_8_out, in_1[0]);
  not not_9 (not_9_out, in_1[2]);
  not not_10 (not_10_out, in_1[1]);
  not not_11 (not_11_out, in_1[3]);
  not not_12 (not_12_out, in_1[0]);
  not not_13 (not_13_out, in_1[3]);
  not not_14 (not_14_out, in_1[1]);
  not not_15 (not_15_out, in_1[2]);
  not not_16 (not_16_out, in_1[1]);
  not not_17 (not_17_out, in_1[2]);
  not not_18 (not_18_out, in_1[0]);
  not not_19 (not_19_out, in_1[1]);
  not not_20 (not_20_out, in_1[0]);
  not not_21 (not_21_out, in_1[3]);
  not not_22 (not_22_out, in_1[2]);
  not not_23 (not_23_out, in_1[0]);
  not not_24 (not_24_out, in_1[1]);
  not not_25 (not_25_out, in_1[0]);
  not not_26 (not_26_out, in_1[3]);
  not not_27 (not_27_out, in_1[2]);
  not not_28 (not_28_out, in_1[3]);
  not not_29 (not_29_out, in_1[2]);
  not not_30 (not_30_out, in_1[0]);
  not not_31 (not_31_out, in_1[3]);
  not not_32 (not_32_out, in_1[2]);
  not not_33 (not_33_out, in_1[1]);
  not not_34 (not_34_out, in_1[0]);
  and and_1 (and_1_out, not_1_out, not_2_out, in_1[0]);
  and and_2 (and_2_out, not_3_out, not_4_out, in_1[1], not_5_out);
  and and_3 (and_3_out, not_6_out, in_1[2], not_7_out, not_8_out);
  and and_4 (and_4_out, in_1[2], in_1[1], in_1[0]);
  and and_5 (and_5_out, in_1[3], not_9_out, not_10_out);
  and and_6 (and_6_out, in_1[3], in_1[2], in_1[1]);
  and and_7 (and_7_out, not_11_out, in_1[1], not_12_out);
  and and_8 (and_8_out, not_13_out, in_1[2], not_14_out, in_1[0]);
  and and_9 (and_9_out, in_1[3], not_15_out, not_16_out);
  and and_10 (and_10_out, in_1[3], not_17_out, not_18_out);
  and and_11 (and_11_out, in_1[3], not_19_out, not_20_out);
  and and_12 (and_12_out, in_1[3], in_1[2], in_1[1], in_1[0]);
  and and_13 (and_13_out, not_21_out, not_22_out, not_23_out);
  and and_14 (and_14_out, not_24_out, not_25_out);
  and and_15 (and_15_out, not_26_out, in_1[2], in_1[0]);
  and and_16 (and_16_out, in_1[3], not_27_out, in_1[1], in_1[0]);
  and and_17 (and_17_out, not_28_out, not_29_out, not_30_out);
  and and_18 (and_18_out, not_31_out, in_1[1]);
  and and_19 (and_19_out, in_1[3], not_32_out, not_33_out, in_1[0]);
  and and_20 (and_20_out, in_1[3], in_1[2], not_34_out);
  or or_1 (out_2[3], and_1_out, and_2_out, and_3_out, and_4_out, and_5_out, and_6_out);
  or or_2 (out_2[2], and_7_out, and_8_out, and_9_out, and_10_out, and_11_out, and_12_out);
  or or_3 (out_2[1], and_13_out, and_14_out, and_15_out, and_16_out);
  or or_4 (out_2[0], and_17_out, and_18_out, and_19_out, and_20_out);
endmodule

module S1 (
  input  [3:0] in_1,
  output [3:0] out_2
);

  wire and_1_out, and_2_out, and_3_out, and_4_out, and_5_out, and_6_out, and_7_out, and_8_out, and_9_out,
       and_10_out, and_11_out, and_12_out, and_13_out, and_14_out, and_15_out, and_16_out, and_17_out,
       and_18_out, and_19_out, and_20_out, and_21_out, not_1_out, not_2_out, not_3_out, not_4_out, not_5_out,
       not_6_out, not_7_out, not_8_out, not_9_out, not_10_out, not_11_out, not_12_out, not_13_out,
       not_14_out, not_15_out, not_16_out, not_17_out, not_18_out, not_19_out, not_20_out, not_21_out,
       not_22_out, not_23_out, not_24_out, not_25_out, not_26_out, not_27_out, not_28_out, not_29_out,
       not_30_out, not_31_out, not_32_out, not_33_out, not_34_out, not_35_out, not_36_out, not_37_out;

  not not_1 (not_1_out, in_1[3]);
  not not_2 (not_2_out, in_1[3]);
  not not_3 (not_3_out, in_1[0]);
  not not_4 (not_4_out, in_1[2]);
  not not_5 (not_5_out, in_1[0]);
  not not_6 (not_6_out, in_1[2]);
  not not_7 (not_7_out, in_1[1]);
  not not_8 (not_8_out, in_1[3]);
  not not_9 (not_9_out, in_1[2]);
  not not_10 (not_10_out, in_1[3]);
  and and_1 (and_1_out, not_10_out, not_11_out, not_12_out);
  not not_11 (not_11_out, in_1[2]);
  not not_12 (not_12_out, in_1[1]);
  not not_13 (not_13_out, in_1[3]);
  not not_14 (not_14_out, in_1[1]);
  and and_2 (and_2_out, not_13_out, not_14_out, not_15_out);
  not not_15 (not_15_out, in_1[0]);
  and and_3 (and_3_out, not_1_out, in_1[2], in_1[1], in_1[0]);
  not not_16 (not_16_out, in_1[1]);
  and and_4 (and_4_out, in_1[3], not_16_out, in_1[0]);
  and and_5 (and_5_out, in_1[3], not_17_out, in_1[1]);
  not not_17 (not_17_out, in_1[2]);
  not not_18 (not_18_out, in_1[3]);
  and and_6 (and_6_out, not_18_out, not_19_out, not_20_out);
  not not_19 (not_19_out, in_1[2]);
  not not_20 (not_20_out, in_1[1]);
  not not_21 (not_21_out, in_1[3]);
  and and_7 (and_7_out, not_21_out, not_22_out, in_1[0]);
  not not_22 (not_22_out, in_1[2]);
  and and_8 (and_8_out, not_2_out, in_1[2], in_1[1], not_3_out);
  and and_9 (and_9_out, in_1[3], not_4_out, in_1[1], not_5_out);
  and and_10 (and_10_out, in_1[3], in_1[2], not_23_out);
  not not_23 (not_23_out, in_1[1]);
  and and_11 (and_11_out, in_1[3], in_1[2], in_1[0]);
  not not_24 (not_24_out, in_1[3]);
  and and_12 (and_12_out, not_24_out, not_25_out, not_26_out);
  not not_25 (not_25_out, in_1[2]);
  not not_26 (not_26_out, in_1[0]);
  not not_27 (not_27_out, in_1[2]);
  and and_13 (and_13_out, not_27_out, in_1[1], not_28_out);
  not not_28 (not_28_out, in_1[0]);
  not not_29 (not_29_out, in_1[3]);
  and and_14 (and_14_out, not_29_out, in_1[1], in_1[0]);
  and and_15 (and_15_out, in_1[3], not_6_out, not_7_out, in_1[0]);
  and and_16 (and_16_out, in_1[3], in_1[2], not_30_out);
  not not_30 (not_30_out, in_1[0]);
  not not_31 (not_31_out, in_1[3]);
  and and_17 (and_17_out, not_31_out, not_32_out, not_33_out);
  not not_32 (not_32_out, in_1[1]);
  not not_33 (not_33_out, in_1[0]);
  and and_18 (and_18_out, not_8_out, not_9_out, in_1[1], in_1[0]);
  and and_19 (and_19_out, in_1[2], in_1[1], not_34_out);
  not not_34 (not_34_out, in_1[0]);
  and and_20 (and_20_out, in_1[3], not_35_out, not_36_out);
  not not_35 (not_35_out, in_1[2]);
  not not_36 (not_36_out, in_1[1]);
  and and_21 (and_21_out, in_1[3], not_37_out, in_1[0]);
  not not_37 (not_37_out, in_1[1]);
  or or_1 (out_2[3], and_1_out, and_2_out, and_3_out, and_4_out, and_5_out);
  or or_2 (out_2[1], and_12_out, and_13_out, and_14_out, and_15_out, and_16_out);
  or or_3 (out_2[0], and_17_out, and_18_out, and_19_out, and_20_out, and_21_out);
  or or_4 (out_2[2], and_6_out, and_7_out, and_8_out, and_9_out, and_10_out, and_11_out);
endmodule

module S2 (
  input  [3:0] in_1,
  output [3:0] out_2
);

  wire and_1_out, and_2_out, and_3_out, and_4_out, and_5_out, and_6_out, and_7_out, and_8_out, and_9_out,
       and_10_out, and_11_out, and_12_out, and_13_out, and_14_out, and_15_out, and_16_out, and_17_out,
       and_18_out, and_19_out, and_20_out, and_21_out, and_22_out, not_1_out, not_2_out, not_3_out,
       not_4_out, not_5_out, not_6_out, not_7_out, not_8_out, not_9_out, not_10_out, not_11_out, not_12_out,
       not_13_out, not_14_out, not_15_out, not_16_out, not_17_out, not_18_out, not_19_out, not_20_out,
       not_21_out, not_22_out, not_23_out, not_24_out, not_25_out, not_26_out, not_27_out, not_28_out,
       not_29_out, not_30_out, not_31_out, not_32_out, not_33_out, not_34_out, not_35_out;

  not not_1 (not_1_out, in_1[2]);
  not not_2 (not_2_out, in_1[1]);
  not not_3 (not_3_out, in_1[0]);
  not not_4 (not_4_out, in_1[3]);
  not not_5 (not_5_out, in_1[1]);
  not not_6 (not_6_out, in_1[3]);
  not not_7 (not_7_out, in_1[2]);
  not not_8 (not_8_out, in_1[0]);
  not not_9 (not_9_out, in_1[3]);
  not not_10 (not_10_out, in_1[1]);
  not not_11 (not_11_out, in_1[2]);
  not not_12 (not_12_out, in_1[0]);
  not not_13 (not_13_out, in_1[3]);
  not not_14 (not_14_out, in_1[2]);
  not not_15 (not_15_out, in_1[0]);
  not not_16 (not_16_out, in_1[2]);
  not not_17 (not_17_out, in_1[0]);
  not not_18 (not_18_out, in_1[3]);
  not not_19 (not_19_out, in_1[2]);
  not not_20 (not_20_out, in_1[1]);
  not not_21 (not_21_out, in_1[2]);
  not not_22 (not_22_out, in_1[0]);
  not not_23 (not_23_out, in_1[3]);
  not not_24 (not_24_out, in_1[0]);
  not not_25 (not_25_out, in_1[3]);
  not not_26 (not_26_out, in_1[3]);
  not not_27 (not_27_out, in_1[2]);
  not not_28 (not_28_out, in_1[3]);
  not not_29 (not_29_out, in_1[3]);
  not not_30 (not_30_out, in_1[1]);
  not not_31 (not_31_out, in_1[0]);
  not not_32 (not_32_out, in_1[2]);
  not not_33 (not_33_out, in_1[1]);
  not not_34 (not_34_out, in_1[1]);
  not not_35 (not_35_out, in_1[0]);
  and and_1 (and_1_out, not_1_out, not_2_out, not_3_out);
  and and_2 (and_2_out, not_4_out, in_1[1], in_1[0]);
  and and_3 (and_3_out, in_1[2], not_5_out, in_1[0]);
  and and_4 (and_4_out, not_6_out, in_1[2], in_1[1]);
  and and_5 (and_5_out, in_1[3], not_7_out, not_8_out);
  and and_6 (and_6_out, not_9_out, not_10_out, in_1[0]);
  and and_7 (and_7_out, not_11_out, in_1[1], not_12_out);
  and and_8 (and_8_out, not_13_out, in_1[2], in_1[0]);
  and and_9 (and_9_out, in_1[3], not_14_out, not_15_out);
  and and_10 (and_10_out, in_1[3], not_16_out, in_1[1]);
  and and_11 (and_11_out, in_1[3], in_1[1], not_17_out);
  and and_12 (and_12_out, not_18_out, not_19_out, not_20_out, in_1[0]);
  and and_13 (and_13_out, not_21_out, in_1[1], not_22_out);
  and and_14 (and_14_out, not_23_out, in_1[2], not_24_out);
  and and_15 (and_15_out, not_25_out, in_1[2], in_1[1]);
  and and_16 (and_16_out, in_1[3], in_1[2], in_1[0]);
  and and_17 (and_17_out, not_26_out, not_27_out, in_1[1]);
  and and_18 (and_18_out, not_28_out, in_1[1], in_1[0]);
  and and_19 (and_19_out, not_29_out, in_1[2], not_30_out, not_31_out);
  and and_20 (and_20_out, in_1[3], not_32_out, not_33_out);
  and and_21 (and_21_out, in_1[3], not_34_out, in_1[0]);
  and and_22 (and_22_out, in_1[3], in_1[2], in_1[1], not_35_out);
  or or_1 (out_2[3], and_1_out, and_2_out, and_3_out, and_4_out, and_5_out);
  or or_2 (out_2[2], and_6_out, and_7_out, and_8_out, and_9_out, and_10_out, and_11_out);
  or or_3 (out_2[1], and_12_out, and_13_out, and_14_out, and_15_out, and_16_out);
  or or_4 (out_2[0], and_17_out, and_18_out, and_19_out, and_20_out, and_21_out, and_22_out);
endmodule

module S3 (
  input  [3:0] in_1,
  output [3:0] out_2
);

  wire and_1_out, and_2_out, and_3_out, and_4_out, and_5_out, and_6_out, and_7_out, and_8_out, and_9_out,
       and_10_out, and_11_out, and_12_out, and_13_out, and_14_out, and_15_out, and_16_out, and_17_out,
       and_18_out, and_19_out, and_20_out, and_21_out, not_1_out, not_2_out, not_3_out, not_4_out, not_5_out,
       not_6_out, not_7_out, not_8_out, not_9_out, not_10_out, not_11_out, not_12_out, not_13_out,
       not_14_out, not_15_out, not_16_out, not_17_out, not_18_out, not_19_out, not_20_out, not_21_out,
       not_22_out, not_23_out, not_24_out, not_25_out, not_26_out, not_27_out, not_28_out, not_29_out,
       not_30_out, not_31_out, not_32_out;

  not not_1 (not_1_out, in_1[3]);
  not not_2 (not_2_out, in_1[2]);
  not not_3 (not_3_out, in_1[3]);
  not not_4 (not_4_out, in_1[2]);
  not not_5 (not_5_out, in_1[3]);
  not not_6 (not_6_out, in_1[1]);
  not not_7 (not_7_out, in_1[1]);
  not not_8 (not_8_out, in_1[0]);
  not not_9 (not_9_out, in_1[3]);
  not not_10 (not_10_out, in_1[2]);
  not not_11 (not_11_out, in_1[1]);
  not not_12 (not_12_out, in_1[3]);
  not not_13 (not_13_out, in_1[0]);
  not not_14 (not_14_out, in_1[0]);
  not not_15 (not_15_out, in_1[2]);
  not not_16 (not_16_out, in_1[1]);
  not not_17 (not_17_out, in_1[0]);
  not not_18 (not_18_out, in_1[3]);
  not not_19 (not_19_out, in_1[2]);
  not not_20 (not_20_out, in_1[1]);
  not not_21 (not_21_out, in_1[2]);
  not not_22 (not_22_out, in_1[0]);
  not not_23 (not_23_out, in_1[3]);
  not not_24 (not_24_out, in_1[1]);
  not not_25 (not_25_out, in_1[1]);
  not not_26 (not_26_out, in_1[3]);
  not not_27 (not_27_out, in_1[2]);
  not not_28 (not_28_out, in_1[0]);
  not not_29 (not_29_out, in_1[3]);
  not not_30 (not_30_out, in_1[2]);
  not not_31 (not_31_out, in_1[1]);
  not not_32 (not_32_out, in_1[0]);
  and and_1 (and_1_out, not_1_out, not_2_out, in_1[0]);
  and and_2 (and_2_out, not_3_out, not_4_out, in_1[1]);
  and and_3 (and_3_out, not_5_out, in_1[2], not_6_out);
  and and_4 (and_4_out, in_1[3], not_7_out, not_8_out);
  and and_5 (and_5_out, in_1[3], in_1[2], in_1[1], in_1[0]);
  and and_6 (and_6_out, not_9_out, not_10_out, not_11_out, in_1[0]);
  and and_7 (and_7_out, not_12_out, in_1[2], not_13_out);
  and and_8 (and_8_out, in_1[2], in_1[1], not_14_out);
  and and_9 (and_9_out, in_1[3], not_15_out, not_16_out, not_17_out);
  and and_10 (and_10_out, in_1[3], in_1[1], in_1[0]);
  and and_11 (and_11_out, in_1[3], in_1[2], in_1[0]);
  and and_12 (and_12_out, not_18_out, not_19_out, not_20_out, in_1[0]);
  and and_13 (and_13_out, not_21_out, in_1[1], not_22_out);
  and and_14 (and_14_out, not_23_out, in_1[2], in_1[1]);
  and and_15 (and_15_out, in_1[3], in_1[2], not_24_out);
  and and_16 (and_16_out, in_1[3], in_1[2], in_1[0]);
  and and_17 (and_17_out, not_25_out, in_1[0]);
  and and_18 (and_18_out, not_26_out, not_27_out, in_1[1], not_28_out);
  and and_19 (and_19_out, not_29_out, in_1[2], in_1[0]);
  and and_20 (and_20_out, in_1[3], not_30_out, not_31_out);
  and and_21 (and_21_out, in_1[3], in_1[2], in_1[1], not_32_out);
  or or_1 (out_2[3], and_1_out, and_2_out, and_3_out, and_4_out, and_5_out);
  or or_2 (out_2[2], and_6_out, and_7_out, and_8_out, and_9_out, and_10_out, and_11_out);
  or or_3 (out_2[1], and_12_out, and_13_out, and_14_out, and_15_out, and_16_out);
  or or_4 (out_2[0], and_17_out, and_18_out, and_19_out, and_20_out, and_21_out);
endmodule

module S4 (
  input  [3:0] in_1,
  output [3:0] out_2
);

  wire and_1_out, and_2_out, and_3_out, and_4_out, and_5_out, and_6_out, and_7_out, and_8_out, and_9_out,
       and_10_out, and_11_out, and_12_out, and_13_out, and_14_out, and_15_out, and_16_out, and_17_out,
       and_18_out, and_19_out, and_20_out, and_21_out, and_22_out, not_1_out, not_2_out, not_3_out,
       not_4_out, not_5_out, not_6_out, not_7_out, not_8_out, not_9_out, not_10_out, not_11_out, not_12_out,
       not_13_out, not_14_out, not_15_out, not_16_out, not_17_out, not_18_out, not_19_out, not_20_out,
       not_21_out, not_22_out, not_23_out, not_24_out, not_25_out, not_26_out, not_27_out, not_28_out,
       not_29_out, not_30_out, not_31_out, not_32_out, not_33_out;

  not not_1 (not_1_out, in_1[3]);
  not not_2 (not_2_out, in_1[2]);
  not not_3 (not_3_out, in_1[1]);
  not not_4 (not_4_out, in_1[3]);
  not not_5 (not_5_out, in_1[1]);
  not not_6 (not_6_out, in_1[0]);
  not not_7 (not_7_out, in_1[2]);
  not not_8 (not_8_out, in_1[1]);
  not not_9 (not_9_out, in_1[0]);
  not not_10 (not_10_out, in_1[1]);
  not not_11 (not_11_out, in_1[3]);
  not not_12 (not_12_out, in_1[2]);
  not not_13 (not_13_out, in_1[1]);
  not not_14 (not_14_out, in_1[3]);
  not not_15 (not_15_out, in_1[2]);
  not not_16 (not_16_out, in_1[2]);
  not not_17 (not_17_out, in_1[1]);
  not not_18 (not_18_out, in_1[0]);
  not not_19 (not_19_out, in_1[0]);
  and and_1 (and_1_out, not_1_out, not_2_out, not_3_out, in_1[0]);
  not not_20 (not_20_out, in_1[3]);
  and and_2 (and_2_out, not_20_out, in_1[1], not_21_out);
  not not_21 (not_21_out, in_1[0]);
  not not_22 (not_22_out, in_1[1]);
  and and_3 (and_3_out, in_1[2], not_22_out, not_23_out);
  not not_23 (not_23_out, in_1[0]);
  and and_4 (and_4_out, in_1[3], in_1[1], in_1[0]);
  and and_5 (and_5_out, in_1[3], in_1[2], not_24_out);
  not not_24 (not_24_out, in_1[1]);
  not not_25 (not_25_out, in_1[2]);
  not not_26 (not_26_out, in_1[1]);
  and and_6 (and_6_out, not_25_out, not_26_out, in_1[0]);
  and and_7 (and_7_out, not_4_out, in_1[2], not_5_out, not_6_out);
  and and_8 (and_8_out, in_1[2], in_1[1], in_1[0]);
  not not_27 (not_27_out, in_1[1]);
  and and_9 (and_9_out, in_1[3], not_27_out, in_1[0]);
  and and_10 (and_10_out, in_1[3], in_1[1], not_28_out);
  not not_28 (not_28_out, in_1[0]);
  not not_29 (not_29_out, in_1[3]);
  and and_11 (and_11_out, not_29_out, not_30_out, in_1[0]);
  not not_30 (not_30_out, in_1[2]);
  not not_31 (not_31_out, in_1[2]);
  and and_12 (and_12_out, not_31_out, in_1[1], in_1[0]);
  not not_32 (not_32_out, in_1[3]);
  and and_13 (and_13_out, not_32_out, in_1[2], in_1[1]);
  and and_14 (and_14_out, in_1[2], in_1[1], not_33_out);
  not not_33 (not_33_out, in_1[0]);
  and and_15 (and_15_out, in_1[3], not_7_out, not_8_out, not_9_out);
  and and_16 (and_16_out, in_1[3], in_1[2], not_10_out, in_1[0]);
  and and_17 (and_17_out, not_11_out, not_12_out, not_13_out);
  and and_18 (and_18_out, not_14_out, not_15_out, in_1[0]);
  and and_19 (and_19_out, not_16_out, not_17_out, in_1[0]);
  and and_20 (and_20_out, in_1[2], in_1[1], not_18_out);
  and and_21 (and_21_out, in_1[3], in_1[2], not_19_out);
  and and_22 (and_22_out, in_1[3], in_1[2], in_1[1]);
  or or_1 (out_2[3], and_1_out, and_2_out, and_3_out, and_4_out, and_5_out);
  or or_2 (out_2[2], and_6_out, and_7_out, and_8_out, and_9_out, and_10_out);
  or or_3 (out_2[0], and_17_out, and_18_out, and_19_out, and_20_out, and_21_out, and_22_out);
  or or_4 (out_2[1], and_11_out, and_12_out, and_13_out, and_14_out, and_15_out, and_16_out);
endmodule

module S5 (
  input  [3:0] in_1,
  output [3:0] out_2
);

  wire and_1_out, and_2_out, and_3_out, and_4_out, and_5_out, and_6_out, and_7_out, and_8_out, and_9_out,
       and_10_out, and_11_out, and_12_out, and_13_out, and_14_out, and_15_out, and_16_out, and_17_out,
       and_18_out, and_19_out, and_20_out, and_21_out, and_22_out, not_1_out, not_2_out, not_3_out,
       not_4_out, not_5_out, not_6_out, not_7_out, not_8_out, not_9_out, not_10_out, not_11_out, not_12_out,
       not_13_out, not_14_out, not_15_out, not_16_out, not_17_out, not_18_out, not_19_out, not_20_out,
       not_21_out, not_22_out, not_23_out, not_24_out, not_25_out, not_26_out, not_27_out, not_28_out,
       not_29_out, not_30_out, not_31_out, not_32_out, not_33_out, not_34_out, not_35_out, not_36_out;

  not not_1 (not_1_out, in_1[3]);
  not not_2 (not_2_out, in_1[2]);
  not not_3 (not_3_out, in_1[1]);
  not not_4 (not_4_out, in_1[0]);
  not not_5 (not_5_out, in_1[3]);
  not not_6 (not_6_out, in_1[3]);
  not not_7 (not_7_out, in_1[3]);
  not not_8 (not_8_out, in_1[2]);
  not not_9 (not_9_out, in_1[1]);
  not not_10 (not_10_out, in_1[0]);
  not not_11 (not_11_out, in_1[3]);
  not not_12 (not_12_out, in_1[2]);
  not not_13 (not_13_out, in_1[1]);
  not not_14 (not_14_out, in_1[3]);
  not not_15 (not_15_out, in_1[1]);
  not not_16 (not_16_out, in_1[0]);
  not not_17 (not_17_out, in_1[3]);
  not not_18 (not_18_out, in_1[0]);
  not not_19 (not_19_out, in_1[1]);
  not not_20 (not_20_out, in_1[3]);
  not not_21 (not_21_out, in_1[2]);
  not not_22 (not_22_out, in_1[0]);
  not not_23 (not_23_out, in_1[3]);
  not not_24 (not_24_out, in_1[2]);
  not not_25 (not_25_out, in_1[1]);
  not not_26 (not_26_out, in_1[1]);
  not not_27 (not_27_out, in_1[0]);
  not not_28 (not_28_out, in_1[3]);
  not not_29 (not_29_out, in_1[2]);
  not not_30 (not_30_out, in_1[1]);
  not not_31 (not_31_out, in_1[3]);
  not not_32 (not_32_out, in_1[2]);
  not not_33 (not_33_out, in_1[2]);
  not not_34 (not_34_out, in_1[1]);
  not not_35 (not_35_out, in_1[0]);
  not not_36 (not_36_out, in_1[0]);
  and and_1 (and_1_out, not_1_out, not_2_out, not_3_out, not_4_out);
  and and_2 (and_2_out, not_5_out, in_1[1], in_1[0]);
  and and_3 (and_3_out, not_6_out, in_1[2], in_1[0]);
  and and_4 (and_4_out, not_7_out, in_1[2], in_1[1]);
  and and_5 (and_5_out, in_1[3], not_8_out, in_1[1]);
  and and_6 (and_6_out, in_1[3], in_1[2], not_9_out, not_10_out);
  and and_7 (and_7_out, not_11_out, not_12_out, not_13_out);
  and and_8 (and_8_out, not_14_out, not_15_out, not_16_out);
  and and_9 (and_9_out, not_17_out, in_1[2], in_1[1], in_1[0]);
  and and_10 (and_10_out, in_1[3], in_1[1], not_18_out);
  and and_11 (and_11_out, in_1[3], in_1[2], not_19_out);
  and and_12 (and_12_out, not_20_out, not_21_out, not_22_out);
  and and_13 (and_13_out, not_23_out, not_24_out, in_1[1]);
  and and_14 (and_14_out, in_1[2], not_25_out, in_1[0]);
  and and_15 (and_15_out, in_1[3], not_26_out, in_1[0]);
  and and_16 (and_16_out, in_1[3], in_1[1], not_27_out);
  and and_17 (and_17_out, not_28_out, not_29_out, not_30_out);
  and and_18 (and_18_out, not_31_out, not_32_out, in_1[0]);
  and and_19 (and_19_out, not_33_out, not_34_out, in_1[0]);
  and and_20 (and_20_out, in_1[2], in_1[1], not_35_out);
  and and_21 (and_21_out, in_1[3], in_1[2], not_36_out);
  and and_22 (and_22_out, in_1[3], in_1[2], in_1[1]);
  or or_1 (out_2[3], and_1_out, and_2_out, and_3_out, and_4_out, and_5_out, and_6_out);
  or or_2 (out_2[2], and_7_out, and_8_out, and_9_out, and_10_out, and_11_out);
  or or_3 (out_2[1], and_12_out, and_13_out, and_14_out, and_15_out, and_16_out);
  or or_4 (out_2[0], and_17_out, and_18_out, and_19_out, and_20_out, and_21_out, and_22_out);
endmodule

module S6 (
  input  [3:0] in_1,
  output [3:0] out_2
);

  wire and_1_out, and_2_out, and_3_out, and_4_out, and_5_out, and_6_out, and_7_out, and_8_out, and_9_out,
       and_10_out, and_11_out, and_12_out, and_13_out, and_14_out, and_15_out, and_16_out, and_17_out,
       and_18_out, and_19_out, and_20_out, and_21_out, and_22_out, not_1_out, not_2_out, not_3_out,
       not_4_out, not_5_out, not_6_out, not_7_out, not_8_out, not_9_out, not_10_out, not_11_out, not_12_out,
       not_13_out, not_14_out, not_15_out, not_16_out, not_17_out, not_18_out, not_19_out, not_20_out,
       not_21_out, not_22_out, not_23_out, not_24_out, not_25_out, not_26_out, not_27_out, not_28_out,
       not_29_out, not_30_out, not_31_out, not_32_out, not_33_out, not_34_out, not_35_out, not_36_out,
       not_37_out, not_38_out;

  not not_1 (not_1_out, in_1[3]);
  not not_2 (not_2_out, in_1[2]);
  not not_3 (not_3_out, in_1[0]);
  not not_4 (not_4_out, in_1[1]);
  not not_5 (not_5_out, in_1[0]);
  not not_6 (not_6_out, in_1[3]);
  not not_7 (not_7_out, in_1[2]);
  not not_8 (not_8_out, in_1[1]);
  not not_9 (not_9_out, in_1[2]);
  not not_10 (not_10_out, in_1[0]);
  not not_11 (not_11_out, in_1[3]);
  not not_12 (not_12_out, in_1[2]);
  not not_13 (not_13_out, in_1[0]);
  not not_14 (not_14_out, in_1[3]);
  not not_15 (not_15_out, in_1[0]);
  not not_16 (not_16_out, in_1[2]);
  not not_17 (not_17_out, in_1[3]);
  not not_18 (not_18_out, in_1[1]);
  not not_19 (not_19_out, in_1[1]);
  not not_20 (not_20_out, in_1[0]);
  not not_21 (not_21_out, in_1[3]);
  not not_22 (not_22_out, in_1[2]);
  not not_23 (not_23_out, in_1[1]);
  not not_24 (not_24_out, in_1[2]);
  not not_25 (not_25_out, in_1[1]);
  not not_26 (not_26_out, in_1[0]);
  not not_27 (not_27_out, in_1[3]);
  not not_28 (not_28_out, in_1[0]);
  not not_29 (not_29_out, in_1[2]);
  not not_30 (not_30_out, in_1[1]);
  not not_31 (not_31_out, in_1[3]);
  not not_32 (not_32_out, in_1[2]);
  not not_33 (not_33_out, in_1[1]);
  not not_34 (not_34_out, in_1[0]);
  not not_35 (not_35_out, in_1[3]);
  not not_36 (not_36_out, in_1[2]);
  not not_37 (not_37_out, in_1[2]);
  not not_38 (not_38_out, in_1[1]);
  and and_1 (and_1_out, not_1_out, not_2_out, in_1[1], not_3_out);
  and and_2 (and_2_out, in_1[2], not_4_out, not_5_out);
  and and_3 (and_3_out, not_6_out, in_1[2], in_1[1], in_1[0]);
  and and_4 (and_4_out, in_1[3], not_7_out, not_8_out);
  and and_5 (and_5_out, in_1[3], not_9_out, in_1[0]);
  and and_6 (and_6_out, in_1[3], in_1[2], not_10_out);
  and and_7 (and_7_out, not_11_out, not_12_out, not_13_out);
  and and_8 (and_8_out, not_14_out, in_1[1], not_15_out);
  and and_9 (and_9_out, not_16_out, in_1[1], in_1[0]);
  and and_10 (and_10_out, not_17_out, in_1[2], not_18_out, in_1[0]);
  and and_11 (and_11_out, in_1[3], not_19_out, not_20_out);
  and and_12 (and_12_out, not_21_out, not_22_out, not_23_out);
  and and_13 (and_13_out, not_24_out, not_25_out, not_26_out);
  and and_14 (and_14_out, not_27_out, in_1[2], in_1[1]);
  and and_15 (and_15_out, in_1[2], in_1[1], not_28_out);
  and and_16 (and_16_out, in_1[3], not_29_out, in_1[1], in_1[0]);
  and and_17 (and_17_out, in_1[3], in_1[2], not_30_out, in_1[0]);
  and and_18 (and_18_out, not_31_out, not_32_out, not_33_out, not_34_out);
  and and_19 (and_19_out, not_35_out, in_1[1], in_1[0]);
  and and_20 (and_20_out, in_1[3], not_36_out, in_1[0]);
  and and_21 (and_21_out, in_1[3], not_37_out, in_1[1]);
  and and_22 (and_22_out, in_1[3], in_1[2], not_38_out);
  or or_1 (out_2[3], and_1_out, and_2_out, and_3_out, and_4_out, and_5_out, and_6_out);
  or or_2 (out_2[2], and_7_out, and_8_out, and_9_out, and_10_out, and_11_out);
  or or_3 (out_2[1], and_12_out, and_13_out, and_14_out, and_15_out, and_16_out, and_17_out);
  or or_4 (out_2[0], and_18_out, and_19_out, and_20_out, and_21_out, and_22_out);
endmodule

module S7 (
  input  [3:0] in_1,
  output [3:0] out_2
);

  wire and_1_out, and_2_out, and_3_out, and_4_out, and_5_out, and_6_out, and_7_out, and_8_out, and_9_out,
       and_10_out, and_11_out, and_12_out, and_13_out, and_14_out, and_15_out, and_16_out, and_17_out,
       and_18_out, and_19_out, and_20_out, and_21_out, and_22_out, not_1_out, not_2_out, not_3_out,
       not_4_out, not_5_out, not_6_out, not_7_out, not_8_out, not_9_out, not_10_out, not_11_out, not_12_out,
       not_13_out, not_14_out, not_15_out, not_16_out, not_17_out, not_18_out, not_19_out, not_20_out,
       not_21_out, not_22_out, not_23_out, not_24_out, not_25_out, not_26_out, not_27_out, not_28_out,
       not_29_out, not_30_out, not_31_out, not_32_out, not_33_out, not_34_out, not_35_out, not_36_out,
       not_37_out;

  not not_1 (not_1_out, in_1[3]);
  not not_2 (not_2_out, in_1[1]);
  not not_3 (not_3_out, in_1[2]);
  not not_4 (not_4_out, in_1[0]);
  not not_5 (not_5_out, in_1[1]);
  not not_6 (not_6_out, in_1[0]);
  not not_7 (not_7_out, in_1[3]);
  not not_8 (not_8_out, in_1[2]);
  not not_9 (not_9_out, in_1[2]);
  not not_10 (not_10_out, in_1[1]);
  not not_11 (not_11_out, in_1[2]);
  not not_12 (not_12_out, in_1[0]);
  not not_13 (not_13_out, in_1[3]);
  not not_14 (not_14_out, in_1[1]);
  not not_15 (not_15_out, in_1[0]);
  not not_16 (not_16_out, in_1[2]);
  not not_17 (not_17_out, in_1[1]);
  not not_18 (not_18_out, in_1[3]);
  not not_19 (not_19_out, in_1[0]);
  not not_20 (not_20_out, in_1[3]);
  not not_21 (not_21_out, in_1[0]);
  not not_22 (not_22_out, in_1[3]);
  not not_23 (not_23_out, in_1[2]);
  not not_24 (not_24_out, in_1[1]);
  not not_25 (not_25_out, in_1[0]);
  not not_26 (not_26_out, in_1[3]);
  not not_27 (not_27_out, in_1[2]);
  not not_28 (not_28_out, in_1[1]);
  not not_29 (not_29_out, in_1[3]);
  not not_30 (not_30_out, in_1[2]);
  not not_31 (not_31_out, in_1[0]);
  not not_32 (not_32_out, in_1[2]);
  not not_33 (not_33_out, in_1[1]);
  not not_34 (not_34_out, in_1[0]);
  not not_35 (not_35_out, in_1[3]);
  not not_36 (not_36_out, in_1[1]);
  not not_37 (not_37_out, in_1[0]);
  and and_1 (and_1_out, not_1_out, not_2_out, in_1[0]);
  and and_2 (and_2_out, not_3_out, in_1[1], not_4_out);
  and and_3 (and_3_out, in_1[2], not_5_out, not_6_out);
  and and_4 (and_4_out, not_7_out, in_1[2], in_1[0]);
  and and_5 (and_5_out, in_1[3], not_8_out, in_1[1]);
  and and_6 (and_6_out, not_9_out, not_10_out, in_1[0]);
  and and_7 (and_7_out, not_11_out, in_1[1], not_12_out);
  and and_8 (and_8_out, not_13_out, in_1[2], not_14_out, not_15_out);
  and and_9 (and_9_out, in_1[3], not_16_out, not_17_out);
  and and_10 (and_10_out, in_1[3], in_1[2], in_1[1]);
  and and_11 (and_11_out, not_18_out, in_1[1], not_19_out);
  and and_12 (and_12_out, not_20_out, in_1[2], not_21_out);
  and and_13 (and_13_out, not_22_out, in_1[2], in_1[1]);
  and and_14 (and_14_out, in_1[3], not_23_out, not_24_out, not_25_out);
  and and_15 (and_15_out, in_1[3], in_1[1], in_1[0]);
  and and_16 (and_16_out, in_1[3], in_1[2], in_1[0]);
  and and_17 (and_17_out, not_26_out, not_27_out, not_28_out);
  and and_18 (and_18_out, not_29_out, not_30_out, not_31_out);
  and and_19 (and_19_out, not_32_out, not_33_out, not_34_out);
  and and_20 (and_20_out, not_35_out, in_1[2], in_1[1], in_1[0]);
  and and_21 (and_21_out, in_1[3], in_1[2], not_36_out);
  and and_22 (and_22_out, in_1[3], in_1[2], not_37_out);
  or or_1 (out_2[3], and_1_out, and_2_out, and_3_out, and_4_out, and_5_out);
  or or_2 (out_2[2], and_6_out, and_7_out, and_8_out, and_9_out, and_10_out);
  or or_3 (out_2[1], and_11_out, and_12_out, and_13_out, and_14_out, and_15_out, and_16_out);
  or or_4 (out_2[0], and_17_out, and_18_out, and_19_out, and_20_out, and_21_out, and_22_out);
endmodule

module P_Box (
  input  [7:0] in_1,
  input  [7:0] in_2,
  input  [7:0] in_3,
  input  [7:0] in_4,
  output [31:0] out_5
);


  assign out_5 = {in_1[7], in_1[3], in_2[7], in_2[3], in_3[7], in_3[3], in_4[7], in_4[3], in_1[6], in_1[2], in_2[6], in_2[2], in_3[6], in_3[2], in_4[6], in_4[2], in_1[5], in_1[1], in_2[5], in_2[1], in_3[5], in_3[1], in_4[5], in_4[1], in_1[4], in_1[0], in_2[4], in_2[0], in_3[4], in_3[0], in_4[4], in_4[0]};
endmodule

module KeySchedule (
  input  [15:0] in_1,
  input  [31:0] in_2,
  input  [31:0] in_3,
  input  [4:0] in_4,
  output [15:0] out_5,
  output [31:0] out_6,
  output [31:0] out_7
);

  S0 s0_1 (.in_1(in_2[30:27]), .out_2(out_5[11:8]));
  S0 s0_2 (.in_1({in_1[2:0], in_2[31]}), .out_2(out_5[15:12]));
  assign out_6[15:11] = {in_2[2:0], in_3[31:30]} ^ in_4;  // XOR_Gate xor_1, 5 bits wide

  assign out_5[7:0] = in_2[26:19];
  assign {out_6[31:16], out_6[10:0]} = {in_2[18:3], in_3[29:19]};
  assign out_7 = {in_3[18:0], in_1[15:3]};
endmodule

module _7Shift (
  input  [31:0] in_1,
  output [31:0] out_2
);


  assign out_2 = {in_1[24:0], in_1[31:25]};
endmodule
