// Logisim project PRESENT.circ as structural Verilog: 11 circuits, main circuit main
module main (
  output [31:0] out_1,
  output [31:0] out_2
);

  wire and_1_out, and_2_out, and_3_out, clock_1_out, multiplexer_1_out, multiplexer_2_out;
  wire [2:0] counter_2_q;
  wire [4:0] adder_1_out, counter_1_q, subtractor_1_out;
  wire [15:0] multiplexer_5_out, multiplexer_5_out_2, multiplexer_8_out, multiplexer_8_out_2,
       multiplexer_9_out, register_7_q, register_8_q, s_box_1_out_5, s_box_1_out_6, s_box_1_out_7,
       s_box_1_out_8;
  wire [31:0] addround_1_out_5, addround_1_out_6, addround_2_out_5, addround_2_out_6, keytransform_1_out_5,
       keytransform_1_out_6, multiplexer_3_out, multiplexer_7_out, multiplexer_10_out, multiplexer_11_out,
       multiplexer_12_out, multiplexer_13_out, multiplexer_14_out, p_box_n_1_out_5, p_box_n_1_out_6,
       ram_1_data, register_1_q, register_2_q, register_3_q, register_4_q, register_5_q, register_6_q,
       register_9_q, register_10_q;
  wire [31:16] keytransform_1_out_7, register_8_q_2;

  and and_1 (and_1_out, counter_2_q[2], counter_2_q[1], ~counter_2_q[0]);  // AND_Gate
  Multiplexer #(.enable("false")) multiplexer_1 (
    .in0(1'b0), .in1(clock_1_out), .out(multiplexer_1_out), .sel(and_1_out));
  Multiplexer #(.enable("false")) multiplexer_2 (
    .in0(multiplexer_1_out), .in1(1'b1), .out(multiplexer_2_out), .sel(and_2_out));
  Clock clock_1 (.out(clock_1_out));
  Counter #(.width(5), .max('h1f)) counter_1 (
    .D(counter_1_q), .count(1'b1), .Q(counter_1_q), .clk(multiplexer_2_out));  // open: load, carry, clr
  Subtractor #(.width(5)) subtractor_1 (.a({5{1'b1}}), .b(counter_1_q), .out(subtractor_1_out));  // open: bin, bout
  Adder #(.width(5)) adder_1 (.a(counter_1_q), .b(5'b00001), .out(adder_1_out));  // open: cin, cout
  // Probe on adder_1_out
  and and_2 (and_2_out, adder_1_out[4], adder_1_out[3], adder_1_out[2], adder_1_out[1], adder_1_out[0]);
  and and_3 (and_3_out, subtractor_1_out[0], subtractor_1_out[1], subtractor_1_out[2], subtractor_1_out[3], subtractor_1_out[4]);
  Register #(.width(32)) register_1 (.D(addround_2_out_6), .Q(register_1_q), .clk(multiplexer_2_out));  // open: en, clr
  // Probe on addround_2_out_6
  Counter #(.width(3), .max('h6), .ongoal("stay"), .trigger("falling")) counter_2 (
    .D(counter_2_q), .count(1'b1), .Q(counter_2_q), .clk(clock_1_out));  // open: load, carry, clr
  Multiplexer #(.select(3), .width(32), .enable("false")) multiplexer_3 (
    .in1(ram_1_data), .out(multiplexer_3_out), .sel(counter_2_q));  // open: in0, in2, in3, in4, in5, in6, in7
  Multiplexer #(.width(32), .enable("false")) multiplexer_4 (
    .in1(addround_2_out_6), .out(out_1), .sel(and_2_out));  // open: in0
  Register #(.width(32)) register_2 (.D(multiplexer_3_out), .Q(register_2_q), .clk(clock_1_out));  // open: en, clr
  AddRound addround_1 (
    .in_3({register_6_q[15:0], register_8_q_2}), .in_4({register_5_q[15:0], register_6_q[31:16]}),
    .in_1(register_2_q), .in_2(register_3_q), .out_6(addround_1_out_6), .out_5(addround_1_out_5));
  Multiplexer #(.width(32), .enable("false")) multiplexer_5 (
    .in0(register_1_q), .in1(addround_1_out_6), .out({multiplexer_5_out_2, multiplexer_5_out}),
    .sel(and_3_out));
  S_box s_box_1 (
    .in_1(multiplexer_5_out_2), .in_2(multiplexer_5_out), .in_3(multiplexer_8_out_2),
    .in_4(multiplexer_8_out), .out_5(s_box_1_out_5), .out_6(s_box_1_out_6), .out_7(s_box_1_out_7),
    .out_8(s_box_1_out_8));
  P_box_n p_box_n_1 (
    .in_1(s_box_1_out_5), .in_2(s_box_1_out_6), .in_3(s_box_1_out_7), .in_4(s_box_1_out_8),
    .out_5(p_box_n_1_out_5), .out_6(p_box_n_1_out_6));
  AddRound addround_2 (
    .in_3({keytransform_1_out_5[15:0], keytransform_1_out_6[31:16]}),
    .in_4({keytransform_1_out_7, keytransform_1_out_5[31:16]}), .in_1(p_box_n_1_out_5),
    .in_2(p_box_n_1_out_6), .out_6(addround_2_out_6), .out_5(addround_2_out_5));
  Multiplexer #(.width(32), .enable("false")) multiplexer_6 (
    .in1(addround_2_out_5), .out(out_2), .sel(and_2_out));  // open: in0
  Multiplexer #(.select(3), .width(32), .enable("false")) multiplexer_7 (
    .in0(ram_1_data), .out(multiplexer_7_out), .sel(counter_2_q));  // open: in1, in2, in3, in4, in5, in6, in7
  Multiplexer #(.width(32), .enable("false")) multiplexer_8 (
    .in0(register_4_q), .in1(addround_1_out_5), .out({multiplexer_8_out_2, multiplexer_8_out}),
    .sel(and_3_out));
  RAM #(.addrWidth(3), .dataWidth(32)) ram_1 (
    .addr(counter_2_q), .data(ram_1_data), .clk(clock_1_out));  // open: sel, ld, clr
  Register #(.width(32), .trigger("falling")) register_3 (
    .D(multiplexer_7_out), .Q(register_3_q), .clk(clock_1_out));  // open: en, clr
  Register #(.width(32)) register_4 (.D(addround_2_out_5), .Q(register_4_q), .clk(multiplexer_2_out));  // open: en, clr
  // Probe on addround_2_out_5
  Multiplexer #(.width(16), .enable("false")) multiplexer_9 (
    .in0(register_7_q), .in1(register_5_q[15:0]), .out(multiplexer_9_out), .sel(and_3_out));
  Multiplexer #(.select(3), .width(32), .enable("false")) multiplexer_10 (
    .in4(ram_1_data), .out(multiplexer_10_out), .sel(counter_2_q));  // open: in0, in1, in2, in3, in5, in6, in7
  Register #(.width(32)) register_5 (.D(multiplexer_10_out), .Q(register_5_q), .clk(clock_1_out));  // open: en, clr
  Multiplexer #(.width(32), .enable("false")) multiplexer_11 (
    .in0(register_9_q), .in1(register_6_q), .out(multiplexer_11_out), .sel(and_3_out));
  KeyTransform keytransform_1 (
    .in_1(multiplexer_9_out), .in_2(multiplexer_11_out), .in_3(multiplexer_13_out),
    .out_7(keytransform_1_out_7), .out_5(keytransform_1_out_5), .out_6(keytransform_1_out_6),
    .in_4(adder_1_out));
  Multiplexer #(.select(3), .width(32), .enable("false")) multiplexer_12 (
    .in3(ram_1_data), .out(multiplexer_12_out), .sel(counter_2_q));  // open: in0, in1, in2, in4, in5, in6, in7
  Register #(.width(32)) register_6 (.D(multiplexer_12_out), .Q(register_6_q), .clk(clock_1_out));  // open: en, clr
  Multiplexer #(.width(32), .enable("false")) multiplexer_13 (
    .in0(register_10_q), .in1({register_8_q_2, register_8_q}), .out(multiplexer_13_out), .sel(and_3_out));
  Register #(.width(16)) register_7 (
    .D(keytransform_1_out_7), .Q(register_7_q), .clk(multiplexer_2_out));  // open: en, clr
  Multiplexer #(.select(3), .width(32), .enable("false")) multiplexer_14 (
    .in2(ram_1_data), .out(multiplexer_14_out), .sel(counter_2_q));  // open: in0, in1, in3, in4, in5, in6, in7
  Register #(.width(32)) register_8 (
    .D(multiplexer_14_out), .Q({register_8_q_2, register_8_q}), .clk(clock_1_out));  // open: en, clr
  Register #(.width(32)) register_9 (
    .D(keytransform_1_out_5), .Q(register_9_q), .clk(multiplexer_2_out));  // open: en, clr
  Register #(.width(32)) register_10 (
    .D(keytransform_1_out_6), .Q(register_10_q), .clk(multiplexer_2_out));  // open: en, clr
endmodule

module S_box (
  input  [15:0] in_1,
  input  [15:0] in_2,
  input  [15:0] in_3,
  input  [15:0] in_4,
  output [15:0] out_5,
  output [15:0] out_6,
  output [15:0] out_7,
  output [15:0] out_8
);

  mini_Sbox s15 (.in_1(in_1[15:12]), .out_2(out_5[15]), .out_3(out_5[14]), .out_4(out_5[13]), .out_5(out_5[12]));
  mini_Sbox s13 (.in_1(in_1[7:4]), .out_2(out_5[7]), .out_3(out_5[6]), .out_4(out_5[5]), .out_5(out_5[4]));
  mini_Sbox s14 (.in_1(in_1[11:8]), .out_2(out_5[11]), .out_3(out_5[10]), .out_4(out_5[9]), .out_5(out_5[8]));
  mini_Sbox s12 (.in_1(in_1[3:0]), .out_2(out_5[3]), .out_3(out_5[2]), .out_4(out_5[1]), .out_5(out_5[0]));
  mini_Sbox s11 (.in_1(in_2[15:12]), .out_2(out_6[15]), .out_3(out_6[14]), .out_4(out_6[13]), .out_5(out_6[12]));
  mini_Sbox s10 (.in_1(in_2[11:8]), .out_2(out_6[11]), .out_3(out_6[10]), .out_4(out_6[9]), .out_5(out_6[8]));
  mini_Sbox s9 (.in_1(in_2[7:4]), .out_2(out_6[7]), .out_3(out_6[6]), .out_4(out_6[5]), .out_5(out_6[4]));
  mini_Sbox s8 (.in_1(in_2[3:0]), .out_2(out_6[3]), .out_3(out_6[2]), .out_4(out_6[1]), .out_5(out_6[0]));
  mini_Sbox s7 (.in_1(in_3[15:12]), .out_2(out_7[15]), .out_3(out_7[14]), .out_4(out_7[13]), .out_5(out_7[12]));
  mini_Sbox s6 (.in_1(in_3[11:8]), .out_2(out_7[11]), .out_3(out_7[10]), .out_4(out_7[9]), .out_5(out_7[8]));
  mini_Sbox s5 (.in_1(in_3[7:4]), .out_2(out_7[7]), .out_3(out_7[6]), .out_4(out_7[5]), .out_5(out_7[4]));
  mini_Sbox s4 (.in_1(in_3[3:0]), .out_2(out_7[3]), .out_3(out_7[2]), .out_4(out_7[1]), .out_5(out_7[0]));
  mini_Sbox s3 (.in_1(in_4[15:12]), .out_2(out_8[15]), .out_3(out_8[14]), .out_4(out_8[13]), .out_5(out_8[12]));
  mini_Sbox s2 (.in_1(in_4[11:8]), .out_2(out_8[11]), .out_3(out_8[10]), .out_4(out_8[9]), .out_5(out_8[8]));
  mini_Sbox s1 (.in_1(in_4[7:4]), .out_2(out_8[7]), .out_3(out_8[6]), .out_4(out_8[5]), .out_5(out_8[4]));
  mini_Sbox s0 (.in_1(in_4[3:0]), .out_2(out_8[3]), .out_3(out_8[2]), .out_4(out_8[1]), .out_5(out_8[0]));
endmodule

module mini_Sbox (
  input  [3:0] in_1,
  output out_2,
  output out_3,
  output out_4,
  output out_5
);

  y3_n y3 (.a(in_1[3]), .b(in_1[2]), .c(in_1[1]), .d(in_1[0]), .x(out_2));
  y2_n y2 (.a(in_1[3]), .b(in_1[2]), .c(in_1[1]), .d(in_1[0]), .x(out_3));
  y1_n y1 (.a(in_1[3]), .b(in_1[2]), .c(in_1[1]), .d(in_1[0]), .x(out_4));
  y0_n y0 (.a(in_1[3]), .b(in_1[2]), .c(in_1[1]), .d(in_1[0]), .x(out_5));
endmodule

module y0_n (
  input  a,
  input  b,
  input  c,
  input  d,
  output x
);

  wire and_1_out, and_2_out, and_3_out, and_4_out, and_5_out, and_6_out, not_1_out, not_2_out, not_3_out,
       not_4_out, not_5_out, not_6_out, not_7_out, not_8_out, not_9_out, not_10_out;

  not not_1 (not_1_out, c);
  not not_2 (not_2_out, b);
  not not_3 (not_3_out, d);
  not not_4 (not_4_out, d);
  not not_5 (not_5_out, a);
  not not_6 (not_6_out, b);
  not not_7 (not_7_out, a);
  not not_8 (not_8_out, a);
  not not_9 (not_9_out, c);
  not not_10 (not_10_out, d);
  and and_1 (and_1_out, a, b, not_1_out, d);
  and and_2 (and_2_out, a, not_2_out, not_3_out);
  and and_3 (and_3_out, a, c, not_4_out);
  and and_4 (and_4_out, not_5_out, not_6_out, d);
  and and_5 (and_5_out, not_7_out, c, d);
  and and_6 (and_6_out, not_8_out, b, not_9_out, not_10_out);
  or or_1 (x, and_1_out, and_2_out, and_3_out, and_4_out, and_5_out, and_6_out);
endmodule

module y1_n (
  input  a,
  input  b,
  input  c,
  input  d,
  output x
);

  wire and_1_out, and_2_out, and_3_out, and_4_out, and_5_out, not_1_out, not_2_out, not_3_out, not_4_out,
       not_5_out, not_6_out, not_7_out;

  not not_1 (not_1_out, b);
  and and_1 (and_1_out, a, not_1_out, not_2_out);
  not not_2 (not_2_out, d);
  and and_2 (and_2_out, a, not_3_out, d);
  not not_3 (not_3_out, c);
  and and_3 (and_3_out, a, b, d);
  not not_4 (not_4_out, a);
  and and_4 (and_4_out, not_4_out, not_5_out, c);
  not not_5 (not_5_out, b);
  not not_6 (not_6_out, a);
  and and_5 (and_5_out, not_6_out, c, not_7_out);
  not not_7 (not_7_out, d);
  or or_1 (x, and_1_out, and_2_out, and_3_out, and_4_out, and_5_out);
endmodule

module y2_n (
  input  a,
  input  b,
  input  c,
  input  d,
  output x
);

  wire and_1_out, and_2_out, and_3_out, and_4_out, and_5_out, not_1_out, not_2_out, not_3_out, not_4_out,
       not_5_out, not_6_out, not_7_out, not_8_out;

  not not_1 (not_1_out, a);
  not not_2 (not_2_out, b);
  not not_3 (not_3_out, c);
  not not_4 (not_4_out, b);
  not not_5 (not_5_out, d);
  not not_6 (not_6_out, c);
  not not_7 (not_7_out, c);
  not not_8 (not_8_out, a);
  and and_1 (and_1_out, not_1_out, not_2_out, not_3_out);
  and and_2 (and_2_out, not_4_out, c, not_5_out);
  and and_3 (and_3_out, a, b, not_6_out);
  and and_4 (and_4_out, a, not_7_out, d);
  and and_5 (and_5_out, not_8_out, b, c, d);
  or or_1 (x, and_1_out, and_2_out, and_3_out, and_4_out, and_5_out);
endmodule

module y3_n (
  input  a,
  input  b,
  input  c,
  input  d,
  output x
);

  wire and_1_out, and_2_out, and_3_out, and_4_out, and_5_out, not_1_out, not_2_out, not_3_out, not_4_out,
       not_5_out, not_6_out, not_7_out;

  not not_1 (not_1_out, a);
  not not_2 (not_2_out, c);
  and and_1 (and_1_out, not_1_out, not_2_out, not_3_out);
  not not_3 (not_3_out, d);
  not not_4 (not_4_out, a);
  and and_2 (and_2_out, not_4_out, c, d);
  not not_5 (not_5_out, a);
  and and_3 (and_3_out, not_5_out, b, c);
  and and_4 (and_4_out, a, not_6_out, d);
  not not_6 (not_6_out, b);
  not not_7 (not_7_out, b);
  and and_5 (and_5_out, a, not_7_out, c);
  or or_1 (x, and_1_out, and_2_out, and_3_out, and_4_out, and_5_out);
endmodule

module P_box (
  input  [3:0] i15,
  input  [3:0] i14,
  input  [3:0] i13,
  input  [3:0] i12,
  input  [3:0] i11,
  input  [3:0] i10,
  input  [3:0] i9,
  input  [3:0] i8,
  input  [3:0] i7,
  input  [3:0] i6,
  input  [3:0] i5,
  input  [3:0] i4,
  input  [3:0] i3,
  input  [3:0] i2,
  input  [3:0] i1,
  input  [3:0] i0,
  output [3:0] p3,
  output [3:0] p2,
  output [3:0] p1,
  output [3:0] p0,
  output [3:0] p7,
  output [3:0] p6,
  output [3:0] p5,
  output [3:0] p4,
  output [3:0] p11,
  output [3:0] p10,
  output [3:0] p9,
  output [3:0] p8,
  output [3:0] p15,
  output [3:0] p14,
  output [3:0] p13,
  output [3:0] p12
);


  assign p0 = {i3[0], i2[0], i1[0], i0[0]};
  assign p1 = {i7[0], i6[0], i5[0], i4[0]};
  assign p2 = {i11[0], i10[0], i9[0], i8[0]};
  assign p3 = {i15[0], i14[0], i13[0], i12[0]};
  assign p4 = {i3[1], i2[1], i1[1], i0[1]};
  assign p5 = {i7[1], i6[1], i5[1], i4[1]};
  assign p6 = {i11[1], i10[1], i9[1], i8[1]};
  assign p7 = {i15[1], i14[1], i13[1], i12[1]};
  assign p8 = {i3[2], i2[2], i1[2], i0[2]};
  assign p9 = {i7[2], i6[2], i5[2], i4[2]};
  assign p10 = {i11[2], i10[2], i9[2], i8[2]};
  assign p11 = {i15[2], i14[2], i13[2], i12[2]};
  assign p12 = {i3[3], i2[3], i1[3], i0[3]};
  assign p13 = {i7[3], i6[3], i5[3], i4[3]};
  assign p14 = {i11[3], i10[3], i9[3], i8[3]};
  assign p15 = {i15[3], i14[3], i13[3], i12[3]};
endmodule

module AddRound (
  input  [31:0] in_1,
  input  [31:0] in_2,
  input  [31:0] in_3,
  input  [31:0] in_4,
  output [31:0] out_5,
  output [31:0] out_6
);

  assign out_6 = in_4 ^ in_1;  // XOR_Gate xor_1, 32 bits wide
  assign out_5 = in_3 ^ in_2;  // XOR_Gate xor_2, 32 bits wide
endmodule

module P_box_n (
  input  [15:0] in_1,
  input  [15:0] in_2,
  input  [15:0] in_3,
  input  [15:0] in_4,
  output [31:0] out_5,
  output [31:0] out_6
);


  assign out_5 = {in_1[15], in_1[11], in_1[7], in_1[3], in_2[15], in_2[11], in_2[7], in_2[3], in_3[15], in_3[11], in_3[7], in_3[3], in_4[15], in_4[11], in_4[7], in_4[3], in_1[14], in_1[10], in_1[6], in_1[2], in_2[14], in_2[10], in_2[6], in_2[2], in_3[14], in_3[10], in_3[6], in_3[2], in_4[14], in_4[10], in_4[6], in_4[2]};
  assign out_6 = {in_1[13], in_1[9], in_1[5], in_1[1], in_2[13], in_2[9], in_2[5], in_2[1], in_3[13], in_3[9], in_3[5], in_3[1], in_4[13], in_4[9], in_4[5], in_4[1], in_1[12], in_1[8], in_1[4], in_1[0], in_2[12], in_2[8], in_2[4], in_2[0], in_3[12], in_3[8], in_3[4], in_3[0], in_4[12], in_4[8], in_4[4], in_4[0]};
endmodule

module KeyTransform (
  input  [15:0] in_1,
  input  [31:0] in_2,
  input  [31:0] in_3,
  input  [4:0] in_4,
  output [31:0] out_5,
  output [31:0] out_6,
  output [15:0] out_7
);

  // Probe on in_3[18:3]
  mini_Sbox mini_sbox_1 (
    .in_1(in_3[18:15]), .out_2(out_7[15]), .out_3(out_7[14]), .out_4(out_7[13]), .out_5(out_7[12]));
  assign out_6[19:15] = in_2[6:2] ^ in_4;  // XOR_Gate xor_1, 5 bits wide

  assign out_5 = {in_3[2:0], in_1, in_2[31:19]};
  assign {out_6[31:20], out_6[14:0]} = {in_2[18:7], in_2[1:0], in_3[31:19]};
  assign out_7[11:0] = in_3[14:3];
endmodule
